# Fritzing sketch Robot_v1 (saved by Fritzing 0.9.6b)
breadboards: 2

parts:
  Part1 = Arduino Uno (Rev3)
  HC-SR04_Sensor_1 = HC-SR04 Ultrasonic Distance Sensor
  Part2 = Arduino Nano (Rev3.0)
  Part5 = NRF24L01+ Breakout Board
  Part6 = Black Joystick KY-023

nets:
  N1: Part1.D12/MISO, HC-SR04_Sensor_1.TRIG
  N2: Part1.D13/SCK, HC-SR04_Sensor_1.ECHO
  GND: Part1.GND, HC-SR04_Sensor_1.GND
  5V: Part1.5V, HC-SR04_Sensor_1.VCC
  GND_2: Part2.GND, Part5.GND, Part6.GND
  N3: Part2.D7, Part5.CE
  N4: Part2.D8, Part5.CS
  N5: Part2.D11/MOSI, Part5.MOSI
  N6: Part2.D12/MISO, Part5.MISO
  5V_2: Part2.5V, Part6.+5V
  N7: Part2.A1, Part6.VRy
  N8: Part2.A0, Part6.VRx
  3V3: Part2.3V3, Part5.VCC
  N9: Part2.D13/SCK, Part5.SCK

notes:
  This ultasonc sensor will be placed on the front of the cart to enssure that collisions do not occur

custom parts:
  Black Joystick KY-023: Description: The joystick is a combination of 2 analoog potentiometer and a digital switch. Arduino GND --> Module pin - Arduino +5V --> Module pin +5V Arduino Analoog 0 --> Module VRx Arduino Analoog 1 --> Module VRy Arduino Digital --> Module SW Dimensions: 1" x 1.25"
